# Fritzing sketch EM_2 (saved by Fritzing 0.9.2b)
circuit board: 6.88566cm x 5.36311cm
breadboards: 2

parts:
  R4 = Resistor [tolerance=±5% resistance=220 package=THT]
  R3 = Trimmer Potentiometer [maximum_resistance=10kΩ package=THT]
  U1 = TEMPERATURE-SENSOR [package=to-92]
  U2 = TEMPERATURE-SENSOR [package=to-92]
  U3 = TEMPERATURE-SENSOR [package=to-92]
  U4 = TEMPERATURE-SENSOR [package=to-92]
  U5 = TEMPERATURE-SENSOR [package=to-92]
  U6 = TEMPERATURE-SENSOR [package=to-92]
  U7 = HALL-EFFECT [package=sc70]
  Arduino1 = Arduino Uno (Rev3)
  LCD1 = LCD screen
  BREAKOUT1 = MAX31850 Thermocouple Breakout
  BREAKOUT2 = MAX31850 Thermocouple Breakout
  BB1 = 4-Line Bi-Directional Level Shifter
  R5 = Resistor [tolerance=±5% resistance=4.7k package=THT]
  S1 = Pushbutton [package="[THT]"]
  R6 = Resistor [tolerance=±5% resistance=10k package=THT]
  R7 = Resistor [tolerance=±5% resistance=4.7k package=THT]
  Raspberry_Pi_A1 = Raspberry Pi A
  BB2 = 4-Line Bi-Directional Level Shifter

nets:
  N1: R4.Pin_0, LCD1.LED+
  VCC: R4.Pin_1, R3.leg2, U1.VCC, U2.VCC, U3.VCC, U4.VCC, U5.VCC, U6.VCC, U7.VCC, Arduino1.5V, LCD1.VDD, BREAKOUT1.VIN, BREAKOUT2.VIN, BB1.HV, S1.Pin_3, S1.Pin_4, R6.Pin_0, R7.Pin_0, BB2.HV
  GND: R3.leg1, U1.GND, U2.GND, U3.GND, U4.GND, U5.GND, U6.GND, U7.GND, Arduino1.GND, LCD1.VSS, LCD1.R/W, LCD1.LED-, BREAKOUT1.GND, BREAKOUT2.GND, BB1.GND, BB2.GND#16
  N2: R3.wiper, LCD1.V0
  N3: U1.ADJ, U2.ADJ, U3.ADJ, U4.ADJ, U5.ADJ, U6.ADJ, Arduino1.D10_PWM/SS, R7.Pin_1
  N4: U7.OUT, Arduino1.D8
  N5: Arduino1.D9_PWM, BB1.B1
  N6: Arduino1.D11_PWM/MOSI, LCD1.E
  N7: Arduino1.D12/MISO, LCD1.RS
  N8: Arduino1.D0/RX, BB2.B2
  N9: Arduino1.D1/TX, BB2.B3
  N10: Arduino1.D2, LCD1.DB7
  N11: Arduino1.D3_PWM, LCD1.DB6
  N12: Arduino1.D4, LCD1.DB5
  N13: Arduino1.D5_PWM, LCD1.DB4
  N14: Arduino1.D7, S1.Pin_1, S1.Pin_2, R6.Pin_1
  N15: Arduino1.3V3, BB1.LV, R5.Pin_1
  N16: BREAKOUT1.DATA, BREAKOUT2.DATA, BB1.A1, R5.Pin_0
  N17: Raspberry_Pi_A1.3V3, BB2.LV
  N18: Raspberry_Pi_A1.GND, BB2.GND#6
  N19: Raspberry_Pi_A1.GPIO_14, BB2.A2
  N20: Raspberry_Pi_A1.GPIO_15, BB2.A3

notes:
  DS18B20 temp sensors:
  Raw water in
  Raw water out
  Coolant entering hx
  Coolant exiting hx
  Cylinder head
  Engine room air
  MAX31850 Thermocouple Amplifier and 1-Wire converter. Thermocouple wires attach to each:
  Oil
  EGT
  Hall Effect RPM Sensor
  10K Pot
  5v to 3.3v converter
  Raspberry PI
  With WiFi - USB
  Dongle

custom parts:
  4-Line Bi-Directional Level Shifter: 4-Channel Bi-Directional Level Shifter
